# Fritzing sketch tapuino-r2 (saved by Fritzing 0.9.1b)
breadboards: 1

parts:
  Part1 = Arduino Nano (Rev3.0)
  microSD1 = MicroSD Breakout  # not connected
  U1 = Optocoupler [package=THT]
  S1 = Pushbutton [package="[THT]"]
  S2 = Pushbutton [package="[THT]"]
  S3 = Pushbutton [package="[THT]"]
  S4 = Pushbutton [package="[THT]"]
  U2 = LCD-16X2 [package=lcd-16x2_noholes]  # not connected
  R7 = Resistor [tolerance=±5% resistance=330 package=THT]
  IC1 = IC, DIP package, 32 pins [chip_label="Imaginary I2C Backpack"]

nets:
  N1: Part1.GND, U1.Pin_2, U1.Pin_4, S1.Pin_1, S1.Pin_2, S2.Pin_1, S2.Pin_2, S3.Pin_1, S3.Pin_2, S4.Pin_1, S4.Pin_2, IC1.pin1
  N2: Part1.D4, U1.Pin_5
  N3: Part1.5V, IC1.pin2
  N4: Part1.A5, IC1.pin3
  N5: Part1.A4, IC1.pin4
  N6: Part1.A3, S1.Pin_3, S1.Pin_4
  N7: Part1.A2, S2.Pin_3, S2.Pin_4
  N8: Part1.A1, S3.Pin_3, S3.Pin_4
  N9: Part1.A0, S4.Pin_3, S4.Pin_4
  N10: U1.Pin_1, R7.Pin_0

notes:
  White = C64 Datasette Read
  Yellow = C64 Datasette Motor
  Blue = C64 Datasette Sense
  Purple = Control 0
  Brown = Control 1
  Green = C64 Datasette Write
  Red = C64 Datasette 5V
  Black = C64 Datasette GND
  I couldn't find a Fritzing part for an I2C backpack. Imagine the connections accordingly :)
  The lower + power rail is actually connected to the C64 Datasette Motor line (yellow)

custom parts:
  MicroSD Breakout: 5V-ready microSD Breakout with Level Shifter
